# Fritzing sketch staci (saved by Fritzing 0.8.5b)
breadboards: 1

parts:
  Part1 = Arduino Mega ADK (Rev3)
  Tiny_RTC1 = Tiny RTC
  S2 = Round Pushbutton
  R1 = Resistor [tolerance=±5% resistance=10k package=THT]

nets:
  5V: Part1.5V, Tiny_RTC1.VCC, S2.leg1
  GND: Part1.GND, Tiny_RTC1.GND, S2.leg0, R1.Pin_1
  N1: Part1.D2_PWM, R1.Pin_0

notes:
  1.8TFT SPI 128*160 v1.1 ST7735
  VCC GND CS RST A0 SDA SCK LED
  I2C: SCL SDA
  Serial MP3 Player
  GND VCC TX RX

custom parts:
  Tiny RTC: Tiny RTC I2C module DS1370Z RTC and AT24C32 EEPROM
